// Logisim project 0-10 Flip Flop.circ as structural Verilog: 1 circuit, main circuit main
module main (
  output Q3,
  output Q2,
  output Q1,
  output Q0
);

  wire and_1_out, and_2_out, clock_1_out, main_1_b, main_1_bl, main_1_br, main_1_m, main_1_t, main_1_tl,
       main_1_tr, not_1_out, not_2_out, or_1_out, or_2_out;

  and and_1 (and_1_out, Q2, Q1, Q0);
  J_K_Flip_Flop j_k_ff_1 (.J(and_1_out), .clk(clock_1_out), .K(Q1), .Q(Q3));  // open: Qn, preset, en, reset
  and and_2 (and_2_out, Q1, Q0);
  J_K_Flip_Flop j_k_ff_2 (.J(and_2_out), .clk(clock_1_out), .K(and_2_out), .Q(Q2));  // open: Qn, preset, en, reset
  Clock clock_1 (.out(clock_1_out));
  or or_1 (or_1_out, Q3, Q0);
  J_K_Flip_Flop j_k_ff_3 (.J(Q0), .clk(clock_1_out), .K(or_1_out), .Q(Q1));  // open: Qn, preset, en, reset
  not not_1 (not_1_out, Q2);
  not not_2 (not_2_out, Q0);
  or or_2 (or_2_out, not_2_out, Q1, not_1_out);
  J_K_Flip_Flop j_k_ff_4 (.J(or_2_out), .clk(clock_1_out), .K(1'b1), .Q(Q0));  // open: Qn, preset, en, reset
  \Decodificador_Binário_para_Algorismo_Decimal_main  main_1 (
    .E8(Q3), .E4(Q2), .E2(Q1), .E1(Q0), .M(main_1_m), .TL(main_1_tl), .T(main_1_t), .TR(main_1_tr),
    .BL(main_1_bl), .B(main_1_b), .BR(main_1_br));
  _7_Segment_Display u_7_segment_display_1 (
    .g(main_1_m), .f(main_1_tl), .a(main_1_t), .b(main_1_tr), .e(main_1_bl), .d(main_1_b), .c(main_1_br));  // open: dp

  // Notes on the sheet:
  //   Q0Q1Q2
  //   Q1
  //   Q0Q1
  //   Q0
  //   Q0+Q3
  //   Q0~ + Q1 + Q2~
endmodule
